# Fritzing sketch TSFRL_master_module (saved by Fritzing 0.9.0b)
circuit board: 6.08472cm x 5.3848cm
perfboards: 1

parts:
  Data = LED - 3mm [color="Yellow (595nm)" package="3 mm [THT]"]
  keyStart = Pushbutton [package="[THT]"]
  keyRight = Pushbutton [package="[THT]"]
  keyReset = Pushbutton [package="[THT]"]
  11_male_pins = male pin header, 11 pins [form="♂ (male)"]
  Error = LED - 3mm [color="Red (660nm)" package="3 mm [THT]"]
  Done = LED - 3mm [color="Green (570nm)" package="3 mm [THT]"]
  keyLeft = Pushbutton [package="[THT]"]
  keyDown = Pushbutton [package="[THT]"]
  Start = LED - 3mm [color="Blue (525nm)" package="3 mm [THT]"]
  keyUp = Pushbutton [package="[THT]"]
  S2 = Pushbutton [package="[THT]"]
  R3 = Resistor [tolerance=±5% resistance=220 package=THT]
  R4 = Resistor [tolerance=±5% resistance=220 package=THT]
  C2 = Ceramic Capacitor [capacitance=100nF package="100 mil [THT, multilayer]"]

nets (from the schematic view):
  GND: Data.cathode, keyStart.Pin_1, keyStart.Pin_2, keyRight.Pin_1, keyRight.Pin_2, keyReset.Pin_1, keyReset.Pin_2, 11_male_pins.pin1, Error.cathode, Done.cathode, keyLeft.Pin_1, keyLeft.Pin_2, keyDown.Pin_1, keyDown.Pin_2, keyUp.Pin_1, keyUp.Pin_2, S2.Pin_3, C2.0
  N1: Data.anode, 11_male_pins.pin8
  N2: keyStart.Pin_3, keyStart.Pin_4, 11_male_pins.pin4
  N3: keyRight.Pin_3, keyRight.Pin_4, 11_male_pins.pin6
  N4: keyReset.Pin_3, keyReset.Pin_4, 11_male_pins.pin2
  N5: 11_male_pins.pin3, keyDown.Pin_3, keyDown.Pin_4
  N6: 11_male_pins.pin5, keyLeft.Pin_3, keyLeft.Pin_4
  N7: 11_male_pins.pin7, keyUp.Pin_3, keyUp.Pin_4
  N8: 11_male_pins.pin9, Error.anode
  N9: 11_male_pins.pin10, Done.anode
  N10: 11_male_pins.pin11, Start.anode
  N11: S2.Pin_1, S2.Pin_2, R3.Pin_0, R4.Pin_0
  5V: R3.Pin_1
  N12: R4.Pin_1, C2.1
